# Fritzing sketch bmw_diagram (saved by Fritzing 0.9.3b)

parts:
  Part1 = Arduino Uno (Rev3)
  L298N1 = L298N DC motor driver
  M1 = DC Motor
  M2 = DC Motor
  Part2 = Bluetooth HC-05 Macho
  M4 = DC Motor  # not connected
  VCC2 = 4 x AAA Battery Mount
  M5 = DC Motor  # not connected
  LED4 = LEDs [package=led10mm]  # not connected
  LED5 = LEDs [package=led10mm]  # not connected
  J1 = Piezo Speaker

nets:
  N1: Part1.D12/MISO, J1.pin2
  GND: Part1.GND, L298N1.GND, Part2.GND, VCC2.-, J1.pin1
  N2: Part1.D0/RX, Part2.TXD
  N3: Part1.D1/TX, Part2.RXD
  N4: Part1.D4, L298N1.IN1
  N5: Part1.D5_PWM, L298N1.IN2
  N6: Part1.D6_PWM, L298N1.IN3
  N7: Part1.D7, L298N1.IN4
  5V: Part1.5V, Part2.VCC
  VIN: Part1.VIN, L298N1.5V
  N8: L298N1.OUT1, M2.pin_2
  N9: L298N1.OUT2, M2.pin_1
  N10: L298N1.OUT3, M1.pin_2
  N11: L298N1.OUT4, M1.pin_1
  N12: L298N1.12V, VCC2.+

custom parts:
  L298N DC motor driver: 2x DC motor driver with 78M05 positive voltage regulator (7..35 V) L298N: max 46 V, 2 A Set 5 V Enable jumper to enable 5 V regultor (needed for the L298N) and +5 V output at screw terminal or supply external +5 V at screw terminal Set ENA and/or ENB to +5 V to enable motor permanently or supply ENA and/or ENB with PWM signal IN1 and IN2 set rotation directory for motor A (OUT1/OUT2) IN2 and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

// code stored in the sketch: BluetoothCar.ino
int in1 = 4;
int in2 = 5;
int in3 = 6;
int in4 = 7;
int val;

void setup() 
{  
  pinMode(in1, OUTPUT);
  pinMode(in2, OUTPUT); 
  pinMode(in3, OUTPUT); 
  pinMode(in4, OUTPUT);
  Serial.begin(9600);
}

void loop()
{
  while (Serial.available() > 0)
  {
    val = Serial.read();
  }
  if( val == 'F') //Forward
    {
      Serial.println("Forward");
      digitalWrite(in1, HIGH);
      digitalWrite(in2, LOW);
      digitalWrite(in3, HIGH);
      digitalWrite(in4, LOW);  
    }
    else if(val == 'B') //Backward
    {
      Serial.println("Reverse");
      digitalWrite(in1, LOW);
      digitalWrite(in2, HIGH);
      digitalWrite(in3, LOW);
      digitalWrite(in4, HIGH); 
    }  
    else if(val == 'L') //Left
    {
      Serial.println("Turn Left");
      digitalWrite(in1, LOW);
      digitalWrite(in2, LOW);
      digitalWrite(in3, HIGH);
      digitalWrite(in4, LOW);
    }
    else if(val == 'R') //Right
    {
      Serial.println("Turn Right");
      digitalWrite(in1, HIGH);
      digitalWrite(in2, LOW);
      digitalWrite(in3, LOW);
      digitalWrite(in4, LOW); 
    }    
    else if(val == 'S') //Stop
    {
      Serial.println("Stop");
      digitalWrite(in1, LOW);
      digitalWrite(in2, LOW);
      digitalWrite(in3, LOW);
      digitalWrite(in4, LOW); 
    }
    else if(val == 'I') //Forward Right
    {
      Serial.println("Forward Right");
      digitalWrite(in1, HIGH);
      digitalWrite(in2, LOW);
      digitalWrite(in3, LOW);
      digitalWrite(in4, LOW);
    }
    else if(val == 'J') //Backward Right
    {
      Serial.println("Backward Right");
      digitalWrite(in1, LOW);
      digitalWrite(in2, LOW);
      digitalWrite(in3, LOW);
      digitalWrite(in4, HIGH);
    }
    else if(val == 'G') //Forward Left
    {
      Serial.println("Forward Left");
      digitalWrite(in1, LOW);
      digitalWrite(in2, LOW);
      digitalWrite(in3, HIGH);
      digitalWrite(in4, LOW);
    }
    else if(val == 'H') //Backward Left
    {
      Serial.println("Backward Left");
      digitalWrite(in1, LOW);
      digitalWrite(in2, HIGH);
      digitalWrite(in3, LOW);
      digitalWrite(in4, LOW); 
    }
}
